// Logisim project CPU.circ as structural Verilog: 2 circuits, main circuit ALU
module main (
);

  wire alu_1_f_out, ALU_EQZERO, ALU_INPUT_SWAP, and_1_out, and_2_out, and_4_out, and_5_out, and_6_out,
       and_7_out, ASLEEP, B2I, BOOTSTRAPPING, CLK, CLK_RAW, comparator_1_eq, comparator_2_eq,
       comparator_3_eq, comparator_4_eq, comparator_5_eq, controlled_buffer_5_out, controlled_buffer_14_out,
       controlled_buffer_15_out, controlled_buffer_28_out, controlled_buffer_29_out, DO_JUMP, FAULT, FAULTED,
       FLAG_BUS, FLAG_REG_A, FLAG_REG_B, HALT, HALTED, I2B, INSN_END, INTERNAL_FLAG_REG_A,
       INTERNAL_FLAG_REG_B, JMP, JMP_IF, JMP_IFN, LOAD_A, LOAD_ALU, LOAD_ALU_FLAG, LOAD_B, LOAD_FLAG_A,
       LOAD_FLAG_B, LOAD_INTERNAL_A, LOAD_INTERNAL_B, LOAD_INTERNAL_FLAG_A, LOAD_INTERNAL_FLAG_B, LOAD_PROG,
       LOAD_RAM, NEXT_INSN, not_1_out, not_2_out, not_3_out, not_5_out, not_6_out, not_7_out, not_8_out,
       not_9_out, not_10_out, or_1_out, or_2_out, or_3_out, or_4_out, or_5_out, or_7_out, or_8_out,
       PROG_NEXT, pull_resistor_1_node, pull_resistor_3_node, pull_resistor_4_node, pull_resistor_10_node,
       PWR, RESET, SLEEP, STORE_A, STORE_ALU_OP, STORE_B, STORE_DISPLAY, STORE_FLAG_A, STORE_FLAG_B,
       STORE_INSN, STORE_INTERNAL_A, STORE_INTERNAL_B, STORE_INTERNAL_FLAG_A, STORE_INTERNAL_FLAG_B,
       STORE_RAM, STORE_RAM_ADDR, SWAP_FLAGS, SWAP_INT, SWAP_INTERNAL_FLAGS, SWAP_INTERNAL_INT, WIRE_FAULT,
       ZERO_FAULT, ZERO_FAULTED;
  wire [1:0] pull_resistor_11_node;
  wire [5:0] bitselector_1_out;
  wire [7:0] pull_resistor_2_node, STEP;
  wire [15:0] alu_1_out, bit_extender_1_out, BUS, controlled_buffer_1_out, controlled_buffer_8_out,
       controlled_buffer_9_out, controlled_buffer_10_out, controlled_buffer_11_out, counter_3_q, DISPLAY,
       INSN, INTERNAL_REG_A, INTERNAL_REG_B, PROG_ADDR, PROG_VALUE, pull_resistor_6_node,
       pull_resistor_16_node, pull_resistor_19_node, REG_A, REG_B, register_1_q, register_2_q, register_8_q;
  wire [31:0] pull_resistor_17_node, pull_resistor_28_node, UPTIME;
  wire [31:10] rom_3_data;

  LED led_1 (.in(PWR));
  ROM #(.addrWidth(16), .dataWidth(16)) rom_1 (.addr(PROG_ADDR), .data(PROG_VALUE));
  or or_1 (or_1_out, PROG_NEXT, NEXT_INSN);
  assign controlled_buffer_1_out = NEXT_INSN ? PROG_VALUE : 16'bz;  // Controlled_Buffer controlled_buffer_1
  or or_2 (or_2_out, NEXT_INSN, INSN_END);
  Pull_Resistor #(.pull(1)) pull_resistor_1 (.node(pull_resistor_1_node));
  Pull_Resistor pull_resistor_2 (.node(pull_resistor_2_node));
  Clock clock_1 (.out(CLK_RAW));
  Button button_1 (.out(RESET));
  // Probe on DISPLAY
  D_Flip_Flop #(.trigger("falling")) d_ff_1 (.D(HALT), .clk(CLK), .Q(HALTED), .reset(RESET));  // open: Qn, preset
  D_Flip_Flop #(.trigger("falling")) d_ff_2 (.D(or_3_out), .clk(CLK), .Q(FAULTED), .reset(RESET));  // open: Qn, preset
  or or_3 (or_3_out, WIRE_FAULT, FAULT);
  D_Flip_Flop #(.trigger("falling")) d_ff_3 (
    .D(ZERO_FAULT), .clk(CLK), .Q(ZERO_FAULTED), .reset(RESET));  // open: Qn, preset
  // ErrorDetector #(.width(16)) errordetector_1: pin names not known; wires that end beside it: BUS, WIRE_FAULT
  // ErrorDetector errordetector_2: pin names not known; wires that end beside it: FLAG_BUS, WIRE_FAULT
  Counter #(.width(16), .max('hffff)) counter_1 (
    .clr(RESET), .load(DO_JUMP), .up(pull_resistor_3_node), .count(or_1_out), .clk(CLK), .D(BUS),
    .Q(PROG_ADDR));  // open: carry
  Pull_Resistor #(.pull(1)) pull_resistor_3 (.node(pull_resistor_3_node));
  Register #(.width(16)) register_1 (
    .D(controlled_buffer_1_out), .en(or_4_out), .clk(CLK), .Q(register_1_q), .clr(RESET));
  assign controlled_buffer_1_out = not_1_out ? BUS : 16'bz;  // Controlled_Buffer controlled_buffer_2
  not not_1 (not_1_out, NEXT_INSN);
  or or_4 (or_4_out, STORE_INSN, NEXT_INSN);
  Counter counter_2 (
    .clr(RESET), .load(or_2_out), .up(pull_resistor_1_node), .count(pull_resistor_1_node), .clk(CLK),
    .D(pull_resistor_2_node), .Q(STEP));  // open: carry
  Counter #(.width(16), .max('hffff)) counter_3 (
    .clr(RESET), .load(SLEEP), .up(pull_resistor_4_node), .count(ASLEEP), .clk(CLK_RAW), .D(BUS),
    .Q(counter_3_q));  // open: carry
  Pull_Resistor pull_resistor_4 (.node(pull_resistor_4_node));
  // Probe on DISPLAY
  // Probe on BUS
  // Probe on FLAG_BUS
  Pull_Resistor pull_resistor_5 (.node(WIRE_FAULT));
  and and_1 (and_1_out, JMP_IF, FLAG_BUS);
  or or_5 (or_5_out, and_1_out, and_2_out);
  and and_2 (and_2_out, ~FLAG_BUS, JMP_IFN);  // AND_Gate
  D_Flip_Flop d_ff_4 (.D(1'b1), .clk(CLK), .Qn(BOOTSTRAPPING), .reset(RESET));  // open: Q, preset
  // Probe on DISPLAY
  LED led_2 (.in(FAULTED));
  LED led_3 (.in(ZERO_FAULTED));
  or or_6 (DO_JUMP, JMP, or_5_out);
  not not_2 (not_2_out, BOOTSTRAPPING);
  assign INSN = not_2_out ? register_1_q : 16'bz;  // Controlled_Buffer controlled_buffer_3
  assign INSN = BOOTSTRAPPING ? {16{1'b1}} : 16'bz;  // Controlled_Buffer controlled_buffer_4
  Pull_Resistor pull_resistor_6 (.node(pull_resistor_6_node));
  not not_3 (not_3_out, ASLEEP);
  assign controlled_buffer_5_out = PWR ? CLK_RAW : 1'bz;  // Controlled_Buffer controlled_buffer_5
  assign CLK = not_3_out ? controlled_buffer_5_out : 1'bz;  // Controlled_Buffer controlled_buffer_6
  Pull_Resistor pull_resistor_7 (.node(LOAD_PROG));
  assign BUS = LOAD_PROG ? PROG_VALUE : 16'bz;  // Controlled_Buffer controlled_buffer_7
  Comparator #(.width(16)) comparator_1 (
    .a(counter_3_q), .b(pull_resistor_6_node), .eq(comparator_1_eq));  // open: gt, lt
  not not_4 (ASLEEP, comparator_1_eq);
  Pull_Resistor pull_resistor_8 (.node(CLK));
  nor nor_1 (PWR, HALTED, ZERO_FAULTED, FAULTED);
  // Probe on UPTIME
  assign controlled_buffer_8_out = not_5_out ? BUS : 16'bz;  // Controlled_Buffer controlled_buffer_8
  not not_5 (not_5_out, SWAP_INT);
  not not_6 (not_6_out, SWAP_INT);
  assign controlled_buffer_9_out = not_6_out ? BUS : 16'bz;  // Controlled_Buffer controlled_buffer_9
  assign controlled_buffer_10_out = ALU_INPUT_SWAP ? REG_A : 16'bz;  // Controlled_Buffer controlled_buffer_10
  assign controlled_buffer_11_out = not_7_out ? REG_A : 16'bz;  // Controlled_Buffer controlled_buffer_11
  assign controlled_buffer_10_out = not_7_out ? REG_B : 16'bz;  // Controlled_Buffer controlled_buffer_12
  assign controlled_buffer_11_out = ALU_INPUT_SWAP ? REG_B : 16'bz;  // Controlled_Buffer controlled_buffer_13
  not not_7 (not_7_out, ALU_INPUT_SWAP);
  Pull_Resistor pull_resistor_9 (.node(ALU_INPUT_SWAP));
  assign controlled_buffer_14_out = ALU_INPUT_SWAP ? FLAG_REG_A : 1'bz;  // Controlled_Buffer controlled_buffer_14
  not not_8 (not_8_out, ALU_INPUT_SWAP);
  assign controlled_buffer_15_out = not_8_out ? FLAG_REG_A : 1'bz;  // Controlled_Buffer controlled_buffer_15
  assign controlled_buffer_14_out = not_8_out ? FLAG_REG_B : 1'bz;  // Controlled_Buffer controlled_buffer_16
  assign controlled_buffer_15_out = ALU_INPUT_SWAP ? FLAG_REG_B : 1'bz;  // Controlled_Buffer controlled_buffer_17
  ROM #(.addrWidth(24), .dataWidth(32)) rom_2 (
    .addr({INSN, STEP}),
    .data({B2I, I2B, STORE_DISPLAY, STORE_ALU_OP, STORE_INTERNAL_FLAG_B, STORE_INTERNAL_FLAG_A, STORE_FLAG_B, STORE_FLAG_A, STORE_INTERNAL_B, STORE_INTERNAL_A, STORE_B, STORE_A, LOAD_ALU_FLAG, LOAD_ALU, LOAD_INTERNAL_FLAG_B, LOAD_INTERNAL_FLAG_A, LOAD_FLAG_B, LOAD_FLAG_A, LOAD_INTERNAL_B, LOAD_INTERNAL_A, LOAD_B, LOAD_A, JMP_IFN, JMP_IF, JMP, STORE_INSN, LOAD_PROG, PROG_NEXT, INSN_END, SLEEP, FAULT, HALT}));
  Counter #(.width(32), .max('hffffffff)) u_UPTIME (
    .clr(RESET), .up(pull_resistor_10_node), .count(pull_resistor_10_node), .clk(CLK_RAW), .Q(UPTIME));  // open: load, D, carry
  Pull_Resistor #(.pull(1)) pull_resistor_10 (.node(pull_resistor_10_node));
  or or_7 (or_7_out, SWAP_INT, STORE_A);
  or or_8 (or_8_out, SWAP_INT, STORE_B);
  Register #(.width(16)) register_2 (.D(BUS), .en(STORE_ALU_OP), .clk(CLK), .Q(register_2_q), .clr(RESET));
  LED led_4 (.in(CLK));
  Register #(.width(16)) register_3 (.D(controlled_buffer_8_out), .en(or_7_out), .clk(CLK), .Q(REG_A), .clr(RESET));
  assign controlled_buffer_9_out = SWAP_INT ? REG_A : 16'bz;  // Controlled_Buffer controlled_buffer_18
  assign controlled_buffer_8_out = SWAP_INT ? REG_B : 16'bz;  // Controlled_Buffer controlled_buffer_19
  Register #(.width(16)) register_4 (.D(controlled_buffer_9_out), .en(or_8_out), .clk(CLK), .Q(REG_B), .clr(RESET));
  Register #(.width(16)) register_5 (.D(BUS), .en(STORE_INTERNAL_A), .clk(CLK), .Q(INTERNAL_REG_A), .clr(RESET));
  Register #(.width(16)) register_6 (.D(BUS), .en(STORE_INTERNAL_B), .clk(CLK), .Q(INTERNAL_REG_B), .clr(RESET));
  BitSelector #(.width(16), .group(6)) bitselector_1 (
    .in(register_2_q), .out(bitselector_1_out), .sel(pull_resistor_11_node));
  Pull_Resistor pull_resistor_11 (.node(pull_resistor_11_node));
  assign BUS = LOAD_A ? REG_A : 16'bz;  // Controlled_Buffer controlled_buffer_20
  Pull_Resistor pull_resistor_12 (.node(LOAD_A));
  assign BUS = LOAD_B ? REG_B : 16'bz;  // Controlled_Buffer controlled_buffer_21
  Pull_Resistor pull_resistor_13 (.node(LOAD_B));
  assign BUS = LOAD_INTERNAL_A ? INTERNAL_REG_A : 16'bz;  // Controlled_Buffer controlled_buffer_22
  Pull_Resistor pull_resistor_14 (.node(LOAD_INTERNAL_A));
  assign BUS = LOAD_INTERNAL_B ? INTERNAL_REG_B : 16'bz;  // Controlled_Buffer controlled_buffer_23
  Pull_Resistor pull_resistor_15 (.node(LOAD_INTERNAL_B));
  LED led_5 (.in(CLK));
  ALU alu_1 (
    .OP(bitselector_1_out), .A(controlled_buffer_11_out), .B(controlled_buffer_10_out), .OUT(alu_1_out),
    .F_OUT(alu_1_f_out), .FLAG_A(controlled_buffer_15_out), .FLAG_B(controlled_buffer_14_out));
  Pull_Resistor pull_resistor_16 (.node(pull_resistor_16_node));
  Pull_Resistor pull_resistor_17 (.node(pull_resistor_17_node));
  Pull_Resistor pull_resistor_18 (.node({B2I, I2B, STORE_DISPLAY, STORE_ALU_OP, STORE_INTERNAL_FLAG_B, STORE_INTERNAL_FLAG_A, STORE_FLAG_B, STORE_FLAG_A, STORE_INTERNAL_B, STORE_INTERNAL_A, STORE_B, STORE_A, LOAD_ALU_FLAG, LOAD_ALU, LOAD_INTERNAL_FLAG_B, LOAD_INTERNAL_FLAG_A, LOAD_FLAG_B, LOAD_FLAG_A, LOAD_INTERNAL_B, LOAD_INTERNAL_A, LOAD_B, LOAD_A, JMP_IFN, JMP_IF, JMP, STORE_INSN, LOAD_PROG, PROG_NEXT, INSN_END, SLEEP, FAULT, HALT}));
  Pull_Resistor pull_resistor_19 (.node(pull_resistor_19_node));
  Pull_Resistor pull_resistor_20 (.node(LOAD_ALU));
  Pull_Resistor pull_resistor_21 (.node(LOAD_ALU_FLAG));
  Pull_Resistor pull_resistor_22 (.node(I2B));
  assign FLAG_BUS = I2B ? ~comparator_2_eq : 1'bz;  // Controlled_Inverter controlled_inverter_1
  Comparator #(.width(16), .mode("unsigned")) comparator_2 (
    .a(BUS), .b(pull_resistor_16_node), .eq(comparator_2_eq));  // open: gt, lt
  Pull_Resistor pull_resistor_23 (.node(B2I));
  assign BUS = B2I ? bit_extender_1_out : 16'bz;  // Controlled_Buffer controlled_buffer_24
  assign bit_extender_1_out = {{15{FLAG_BUS}}, FLAG_BUS};  // Bit_Extender bit_extender_1
  Comparator #(.width(32), .mode("unsigned")) comparator_3 (
    .a(pull_resistor_17_node),
    .b({B2I, I2B, STORE_DISPLAY, STORE_ALU_OP, STORE_INTERNAL_FLAG_B, STORE_INTERNAL_FLAG_A, STORE_FLAG_B, STORE_FLAG_A, STORE_INTERNAL_B, STORE_INTERNAL_A, STORE_B, STORE_A, LOAD_ALU_FLAG, LOAD_ALU, LOAD_INTERNAL_FLAG_B, LOAD_INTERNAL_FLAG_A, LOAD_FLAG_B, LOAD_FLAG_A, LOAD_INTERNAL_B, LOAD_INTERNAL_A, LOAD_B, LOAD_A, JMP_IFN, JMP_IF, JMP, STORE_INSN, LOAD_PROG, PROG_NEXT, INSN_END, SLEEP, FAULT, HALT}),
    .eq(comparator_3_eq));  // open: gt, lt
  Comparator #(.width(16), .mode("unsigned")) comparator_4 (
    .a(pull_resistor_19_node), .b(alu_1_out), .eq(comparator_4_eq));  // open: gt, lt
  assign FLAG_BUS = ALU_EQZERO ? comparator_4_eq : 1'bz;  // Controlled_Buffer controlled_buffer_25
  assign BUS = LOAD_ALU ? alu_1_out : 16'bz;  // Controlled_Buffer controlled_buffer_26
  assign FLAG_BUS = LOAD_ALU_FLAG ? alu_1_f_out : 1'bz;  // Controlled_Buffer controlled_buffer_27
  Register #(.width(16)) register_7 (.D(BUS), .en(STORE_DISPLAY), .clk(CLK), .Q(DISPLAY), .clr(RESET));
  Register #(.width(16)) register_8 (.D(BUS), .en(STORE_RAM_ADDR), .clk(CLK), .Q(register_8_q), .clr(RESET));
  LED led_6 (.in(HALT));
  LED led_7 (.in(FAULT));
  LED led_8 (.in(SLEEP));
  LED led_9 (.in(INSN_END));
  LED led_10 (.in(PROG_NEXT));
  LED led_11 (.in(LOAD_PROG));
  LED led_12 (.in(STORE_INSN));
  LED led_13 (.in(JMP));
  LED led_14 (.in(JMP_IF));
  LED led_15 (.in(JMP_IFN));
  LED led_16 (.in(LOAD_A));
  LED led_17 (.in(LOAD_B));
  LED led_18 (.in(LOAD_INTERNAL_A));
  LED led_19 (.in(LOAD_INTERNAL_B));
  LED led_20 (.in(LOAD_FLAG_A));
  LED led_21 (.in(LOAD_FLAG_B));
  LED led_22 (.in(LOAD_INTERNAL_FLAG_A));
  LED led_23 (.in(LOAD_INTERNAL_FLAG_B));
  LED led_24 (.in(LOAD_ALU));
  LED led_25 (.in(LOAD_ALU_FLAG));
  LED led_26 (.in(STORE_A));
  LED led_27 (.in(STORE_B));
  LED led_28 (.in(STORE_INTERNAL_A));
  LED led_29 (.in(STORE_INTERNAL_B));
  LED led_30 (.in(STORE_FLAG_A));
  LED led_31 (.in(STORE_FLAG_B));
  LED led_32 (.in(STORE_INTERNAL_FLAG_A));
  LED led_33 (.in(STORE_INTERNAL_FLAG_B));
  LED led_34 (.in(STORE_ALU_OP));
  LED led_35 (.in(STORE_DISPLAY));
  LED led_36 (.in(I2B));
  LED led_37 (.in(B2I));
  RAM #(.addrWidth(16), .dataWidth(16)) ram_1 (
    .addr(register_8_q), .we(STORE_RAM), .oe(LOAD_RAM), .clk(CLK), .data(BUS));
  and and_3 (ZERO_FAULT, comparator_3_eq, comparator_5_eq);
  and and_4 (and_4_out, CLK, STORE_FLAG_A);
  ROM #(.addrWidth(24), .dataWidth(32)) rom_3 (
    .addr({INSN, STEP}),
    .data({rom_3_data, ALU_EQZERO, NEXT_INSN, LOAD_RAM, STORE_RAM, STORE_RAM_ADDR, ALU_INPUT_SWAP, SWAP_INTERNAL_FLAGS, SWAP_INTERNAL_INT, SWAP_FLAGS, SWAP_INT}));
  assign controlled_buffer_28_out = not_9_out ? FLAG_BUS : 1'bz;  // Controlled_Buffer controlled_buffer_28
  not not_9 (not_9_out, SWAP_FLAGS);
  not not_10 (not_10_out, SWAP_FLAGS);
  assign controlled_buffer_29_out = not_10_out ? FLAG_BUS : 1'bz;  // Controlled_Buffer controlled_buffer_29
  and and_5 (and_5_out, CLK, STORE_FLAG_B);
  D_Flip_Flop d_ff_5 (
    .D(controlled_buffer_28_out), .clk(and_4_out), .Q(FLAG_REG_A), .reset(RESET));  // open: Qn, preset
  assign controlled_buffer_28_out = SWAP_FLAGS ? FLAG_REG_A : 1'bz;  // Controlled_Buffer controlled_buffer_30
  assign controlled_buffer_29_out = SWAP_FLAGS ? FLAG_REG_B : 1'bz;  // Controlled_Buffer controlled_buffer_31
  D_Flip_Flop d_ff_6 (
    .D(controlled_buffer_29_out), .clk(and_5_out), .Q(FLAG_REG_B), .reset(RESET));  // open: Qn, preset
  D_Flip_Flop d_ff_7 (.D(FLAG_BUS), .clk(and_6_out), .Q(INTERNAL_FLAG_REG_A), .reset(RESET));  // open: Qn, preset
  and and_6 (and_6_out, CLK, STORE_INTERNAL_FLAG_A);
  D_Flip_Flop d_ff_8 (.D(FLAG_BUS), .clk(and_7_out), .Q(INTERNAL_FLAG_REG_B), .reset(RESET));  // open: Qn, preset
  and and_7 (and_7_out, CLK, STORE_INTERNAL_FLAG_B);
  assign FLAG_BUS = LOAD_FLAG_A ? FLAG_REG_A : 1'bz;  // Controlled_Buffer controlled_buffer_32
  Pull_Resistor pull_resistor_24 (.node(LOAD_FLAG_A));
  assign FLAG_BUS = LOAD_FLAG_B ? FLAG_REG_B : 1'bz;  // Controlled_Buffer controlled_buffer_33
  Pull_Resistor pull_resistor_25 (.node(LOAD_FLAG_B));
  assign FLAG_BUS = LOAD_INTERNAL_FLAG_A ? INTERNAL_FLAG_REG_A : 1'bz;  // Controlled_Buffer controlled_buffer_34
  Pull_Resistor pull_resistor_26 (.node(LOAD_INTERNAL_FLAG_A));
  assign FLAG_BUS = LOAD_INTERNAL_FLAG_B ? INTERNAL_FLAG_REG_B : 1'bz;  // Controlled_Buffer controlled_buffer_35
  Pull_Resistor pull_resistor_27 (.node(LOAD_INTERNAL_FLAG_B));
  Pull_Resistor pull_resistor_28 (.node(pull_resistor_28_node));
  Pull_Resistor pull_resistor_29 (.node({rom_3_data, ALU_EQZERO, NEXT_INSN, LOAD_RAM, STORE_RAM, STORE_RAM_ADDR, ALU_INPUT_SWAP, SWAP_INTERNAL_FLAGS, SWAP_INTERNAL_INT, SWAP_FLAGS, SWAP_INT}));
  Comparator #(.width(32), .mode("unsigned")) comparator_5 (
    .a(pull_resistor_28_node),
    .b({rom_3_data, ALU_EQZERO, NEXT_INSN, LOAD_RAM, STORE_RAM, STORE_RAM_ADDR, ALU_INPUT_SWAP, SWAP_INTERNAL_FLAGS, SWAP_INTERNAL_INT, SWAP_FLAGS, SWAP_INT}),
    .eq(comparator_5_eq));  // open: gt, lt
  LED led_38 (.in(SWAP_INT));
  LED led_39 (.in(SWAP_FLAGS));
  LED led_40 (.in(SWAP_INTERNAL_INT));
  LED led_41 (.in(SWAP_INTERNAL_FLAGS));
  LED led_42 (.in(ALU_INPUT_SWAP));
  LED led_43 (.in(STORE_RAM_ADDR));
  LED led_44 (.in(STORE_RAM));
  LED led_45 (.in(LOAD_RAM));
  LED led_46 (.in(NEXT_INSN));
  LED led_47 (.in(ALU_EQZERO));

  // Notes on the sheet:
  //   contents of rom_1 (hex, n*v repeats v):
  //   140 1 120 6 141 1 131 6 74 12 10 54 4 2 24 6 80 24 2 0 34 2 24 6 50 24 2 0 2
  //   Halt
  //   Fault
  //   Zero Fault
  //   Program ROM
  //   Program Counter
  //   Instruction register
  //   Step Counter
  //   Sleep Timer
  //   Normal
  //   BUS
  //   DISPLAY
  //   FAULT
  //   Microcode == 0
  //   UPTIME
  //   contents of rom_2 (hex, n*v repeats v):
  //   1 4095*0 404 255*0 804 255*0 10000030 40004 254*0 10000030 40004 254*0 34 255*0 80004004 255*0
  //   80008004 255*0 30 4 2302*0 480 255*0 880 255*0 10000030 40080 254*0 10000030 40080 254*0 b0 255*0
  //   80004080 255*0 80008080 255*0 30 80 2302*0 4500 255*0 4900 255*0 10000030 44100 254*0 10000030 44100
  //   254*0 4130 255*0 80004100 255*0 8000c100 255*0 30 4100 2302*0 4600 255*0 4a00 255*0 10000030 44200
  //   254*0 10000030 44200 254*0 4230 255*0 80004200 255*0 8000c200 255*0 30 4200 2302*0 10000030 500
  //   254*0 10000030 900 254*0 10000030 10000030 40100 253*0 10000030 10000030 40100 253*0 10000030 130
  //   254*0 10000030 80004100 254*0 10000030 80008100 254*0 10000030 30 100 2301*0 10000030 600 254*0
  //   10000030 a00 254*0 10000030 10000030 40200 253*0 10000030 10000030 40200 253*0 10000030 230 254*0
  //   10000030 80004200 254*0 10000030 80008200 254*0 10000030 30 200 2301*0 10000030 80500 254*0 10000030
  //   80900 254*0 10000030 10000030 c0100 253*0 10000030 10000030 c0100 253*0 10000030 80130 254*0
  //   10000030 80084100 254*0 10000030 80088100 254*0 10000030 30 80100 2301*0 20000400 255*0 20000800
  //   255*0 10000030 20040000 254*0 10000030 20040000 254*0 20000030 255*0 a0004000 255*0 a0008000 255*0
  //   30 20000000 30974*0 100400 255*0 200400 255*0 400400 30 1000 3581*0 100800 255*0 200800 255*0 400800
  //   30 1000 3581*0 10000030 140000 254*0 10000030 240000 254*0 10000030 440000 30 1000 3580*0 10000030
  //   140000 254*0 10000030 240000 254*0 10000030 440000 30 1000 3580*0 100030 255*0 200030 255*0 400030
  //   30 1000 3581*0 80104000 255*0 80204000 255*0 80404000 30 1000 3581*0 80108000 255*0 80208000 255*0
  //   80408000 30 1000 3581*0 30 100000 254*0 30 200000 254*0 30 400000 30 1000 36348*0 1004000 255*0
  //   2004000 3839*0 1008000 255*0 2008000 3839*0 10000030 1080000 254*0 10000030 2080000 3838*0 10000030
  //   1080000 254*0 10000030 2080000 3838*0 41000030 255*0 42000030 3839*0 41000400 255*0 42000400 3839*0
  //   41000800 255*0 42000800
  //   Microcode
  //   ALU
  //   Registers
  //   Internal Registers (for use by microcode only)
  //   Display
  //   contents of rom_3 (hex, n*v repeats v):
  //   0 100 254*0 100 255*0 101 255*0 102 3328*0 100 255*0 100 256*0 100 254*0 10 100 254*0 100 255*0 100
  //   255*0 100 254*0 20 80 100 2301*0 100 255*0 100 256*0 100 255*0 110 255*0 100 254*0 100 255*0 100
  //   255*0 20 180 2302*0 100 255*0 100 256*0 100 255*0 110 255*0 100 254*0 100 255*0 100 255*0 20 180
  //   2302*0 100 255*0 100 256*0 100 255*0 110 255*0 100 254*0 100 255*0 100 255*0 20 180 2303*0 300 255*0
  //   300 256*0 300 255*0 310 254*0 200 100 254*0 300 255*0 300 255*0 20 380 2302*0 300 255*0 300 256*0
  //   300 255*0 310 254*0 200 100 254*0 300 255*0 300 255*0 20 380 2302*0 100 255*0 100 256*0 100 255*0
  //   110 255*0 100 254*0 100 255*0 100 255*0 20 180 2301*0 100 255*0 100 256*0 100 255*0 110 255*0 100
  //   254*0 100 255*0 100 255*0 20 180 30974*0 100 255*0 100 256*0 20 140 3581*0 100 255*0 100 256*0 20
  //   140 3582*0 100 255*0 100 256*0 20 140 3581*0 110 255*0 110 255*0 10 20 140 3581*0 100 255*0 100
  //   255*0 20 40 100 3580*0 100 255*0 100 256*0 20 140 3581*0 100 255*0 100 256*0 20 140 3581*0 20 180
  //   254*0 20 180 254*0 20 80 20 140 36348*0 100 255*0 100 3839*0 100 255*0 100 3840*0 100 255*0 100
  //   3839*0 110 255*0 110 3839*0 100 255*0 100 3838*0 100 255*0 100 3839*0 100 255*0 100 16621055*0 100
  //   NO-DRAW ZONE
  //   Look over here for faster simulation
endmodule

module ALU (
  input  [5:0] OP,
  input  [15:0] A,
  input  [15:0] B,
  input  FLAG_A,
  input  FLAG_B,
  output [15:0] OUT,
  output F_OUT
);

  wire adder_1_cout, adder_2_cout, and_2_out, comparator_1_eq, comparator_1_gt, comparator_1_lt,
       comparator_2_eq, comparator_2_gt, comparator_2_lt, decoder_1_out0, decoder_1_out1, decoder_1_out2,
       decoder_1_out3, decoder_1_out4, decoder_1_out5, decoder_1_out6, decoder_1_out7, decoder_1_out8,
       decoder_1_out9, decoder_1_out10, decoder_1_out11, decoder_1_out12, decoder_1_out13, decoder_1_out14,
       decoder_1_out15, decoder_1_out16, decoder_1_out17, decoder_1_out18, decoder_1_out19, decoder_1_out20,
       decoder_1_out21, decoder_1_out22, decoder_1_out23, decoder_1_out24, decoder_1_out25, nand_2_out,
       nor_2_out, not_2_out, not_3_out, or_2_out, pull_resistor_7_node, pull_resistor_8_node,
       pull_resistor_11_node, pull_resistor_13_node, subtractor_1_bout, subtractor_2_bout, xnor_2_out,
       xor_2_out;
  wire [1:0] pull_resistor_5_node, pull_resistor_6_node;
  wire [3:0] bitselector_1_out, bitselector_2_out;
  wire [4:0] bitadder_1_out;
  wire [15:0] adder_1_out, adder_2_out, and_1_out, bit_extender_1_out, divider_1_out, divider_1_rem,
       multiplier_1_out, nand_1_out, negator_1_out, nor_1_out, not_1_out, or_1_out, pull_resistor_9_node,
       pull_resistor_10_node, pull_resistor_12_node, pull_resistor_14_node, pull_resistor_15_node,
       shifter_1_out, shifter_2_out, subtractor_1_out, subtractor_2_out, xnor_1_out, xor_1_out;

  Pull_Resistor pull_resistor_1 (.node(FLAG_A));
  Pull_Resistor pull_resistor_2 (.node(B));
  Pull_Resistor pull_resistor_3 (.node(FLAG_B));
  Pull_Resistor pull_resistor_4 (.node(A));
  Pull_Resistor pull_resistor_5 (.node(pull_resistor_5_node));
  Pull_Resistor pull_resistor_6 (.node(pull_resistor_6_node));
  Pull_Resistor pull_resistor_7 (.node(pull_resistor_7_node));
  Pull_Resistor pull_resistor_8 (.node(pull_resistor_8_node));
  Pull_Resistor pull_resistor_9 (.node(pull_resistor_9_node));
  Pull_Resistor pull_resistor_10 (.node(pull_resistor_10_node));
  Pull_Resistor #(.pull(1)) pull_resistor_11 (.node(pull_resistor_11_node));
  Pull_Resistor pull_resistor_12 (.node(pull_resistor_12_node));
  Pull_Resistor #(.pull(1)) pull_resistor_13 (.node(pull_resistor_13_node));
  Pull_Resistor pull_resistor_14 (.node(pull_resistor_14_node));
  BitSelector #(.width(16), .group(4)) bitselector_1 (.in(B), .out(bitselector_1_out), .sel(pull_resistor_5_node));
  BitSelector #(.width(16), .group(4)) bitselector_2 (.in(B), .out(bitselector_2_out), .sel(pull_resistor_6_node));
  Pull_Resistor pull_resistor_15 (.node(pull_resistor_15_node));
  Pull_Resistor pull_resistor_16 (.node(OP));
  Adder #(.width(16)) adder_1 (.a(A), .b(B), .out(adder_1_out), .cin(pull_resistor_7_node), .cout(adder_1_cout));
  Subtractor #(.width(16)) subtractor_1 (
    .a(A), .b(B), .out(subtractor_1_out), .bin(pull_resistor_8_node), .bout(subtractor_1_bout));
  Multiplier #(.width(16)) multiplier_1 (
    .a(A), .b(B), .out(multiplier_1_out), .cin(pull_resistor_9_node));  // open: cout
  Divider #(.width(16)) divider_1 (
    .a(A), .b(B), .out(divider_1_out), .upper(pull_resistor_10_node), .rem(divider_1_rem));
  Negator #(.width(16)) negator_1 (.in(A), .out(negator_1_out));
  Adder #(.width(16)) adder_2 (
    .a(A), .b(pull_resistor_12_node), .out(adder_2_out), .cin(pull_resistor_11_node), .cout(adder_2_cout));
  Subtractor #(.width(16)) subtractor_2 (
    .a(A), .b(pull_resistor_14_node), .out(subtractor_2_out), .bin(pull_resistor_13_node),
    .bout(subtractor_2_bout));
  Shifter #(.width(16)) shifter_1 (.in(A), .\dist (bitselector_1_out), .out(shifter_1_out));
  Shifter #(.width(16), .shift("lr")) shifter_2 (.in(A), .\dist (bitselector_2_out), .out(shifter_2_out));
  BitAdder #(.width(16)) bitadder_1 (.in0(A), .out(bitadder_1_out));
  assign not_1_out = ~A;  // NOT_Gate not_1, 16 bits wide
  assign and_1_out = A & B;  // AND_Gate and_1, 16 bits wide
  assign or_1_out = A | B;  // OR_Gate or_1, 16 bits wide
  assign xor_1_out = A ^ B;  // XOR_Gate xor_1, 16 bits wide
  assign nand_1_out = ~(A & B);  // NAND_Gate nand_1, 16 bits wide
  assign nor_1_out = ~(A | B);  // NOR_Gate nor_1, 16 bits wide
  assign xnor_1_out = ~(A ^ B);  // XNOR_Gate xnor_1, 16 bits wide
  Comparator #(.width(16)) comparator_1 (
    .a(A), .b(B), .gt(comparator_1_gt), .eq(comparator_1_eq), .lt(comparator_1_lt));
  Comparator #(.width(16)) comparator_2 (
    .a(A), .b(pull_resistor_15_node), .gt(comparator_2_gt), .eq(comparator_2_eq), .lt(comparator_2_lt));
  not not_2 (not_2_out, FLAG_A);
  and and_2 (and_2_out, FLAG_A, FLAG_B);
  or or_2 (or_2_out, FLAG_A, FLAG_B);
  xor xor_2 (xor_2_out, FLAG_A, FLAG_B);
  nand nand_2 (nand_2_out, FLAG_A, FLAG_B);
  nor nor_2 (nor_2_out, FLAG_A, FLAG_B);
  xnor xnor_2 (xnor_2_out, FLAG_A, FLAG_B);
  not not_3 (not_3_out, OP[5]);
  Decoder #(.select(5)) decoder_1 (
    .out0(decoder_1_out0), .out1(decoder_1_out1), .out2(decoder_1_out2), .out3(decoder_1_out3),
    .out4(decoder_1_out4), .out5(decoder_1_out5), .out6(decoder_1_out6), .out7(decoder_1_out7),
    .out8(decoder_1_out8), .out9(decoder_1_out9), .out10(decoder_1_out10), .out11(decoder_1_out11),
    .out12(decoder_1_out12), .out13(decoder_1_out13), .out14(decoder_1_out14), .out15(decoder_1_out15),
    .out16(decoder_1_out16), .out17(decoder_1_out17), .out18(decoder_1_out18), .out19(decoder_1_out19),
    .out20(decoder_1_out20), .out21(decoder_1_out21), .out22(decoder_1_out22), .out23(decoder_1_out23),
    .out24(decoder_1_out24), .out25(decoder_1_out25), .sel(OP[4:0]), .en(not_3_out));  // open: out26, out27, out28, out29, out30, out31
  assign OUT = decoder_1_out0 ? adder_1_out : 16'bz;  // Controlled_Buffer controlled_buffer_1
  assign F_OUT = decoder_1_out0 ? adder_1_cout : 1'bz;  // Controlled_Buffer controlled_buffer_2
  assign OUT = decoder_1_out1 ? subtractor_1_out : 16'bz;  // Controlled_Buffer controlled_buffer_3
  assign F_OUT = decoder_1_out1 ? subtractor_1_bout : 1'bz;  // Controlled_Buffer controlled_buffer_4
  assign OUT = decoder_1_out2 ? multiplier_1_out : 16'bz;  // Controlled_Buffer controlled_buffer_5
  assign OUT = decoder_1_out3 ? divider_1_out : 16'bz;  // Controlled_Buffer controlled_buffer_6
  assign OUT = decoder_1_out4 ? divider_1_rem : 16'bz;  // Controlled_Buffer controlled_buffer_7
  assign OUT = decoder_1_out5 ? negator_1_out : 16'bz;  // Controlled_Buffer controlled_buffer_8
  assign OUT = decoder_1_out6 ? adder_2_out : 16'bz;  // Controlled_Buffer controlled_buffer_9
  assign F_OUT = decoder_1_out6 ? adder_2_cout : 1'bz;  // Controlled_Buffer controlled_buffer_10
  assign OUT = decoder_1_out7 ? subtractor_2_out : 16'bz;  // Controlled_Buffer controlled_buffer_11
  assign F_OUT = decoder_1_out7 ? subtractor_2_bout : 1'bz;  // Controlled_Buffer controlled_buffer_12
  assign OUT = decoder_1_out8 ? shifter_1_out : 16'bz;  // Controlled_Buffer controlled_buffer_13
  assign OUT = decoder_1_out9 ? shifter_2_out : 16'bz;  // Controlled_Buffer controlled_buffer_14
  assign OUT = decoder_1_out10 ? bit_extender_1_out : 16'bz;  // Controlled_Buffer controlled_buffer_15
  assign bit_extender_1_out = {{11{bitadder_1_out[4]}}, bitadder_1_out};  // Bit_Extender bit_extender_1
  assign OUT = decoder_1_out11 ? not_1_out : 16'bz;  // Controlled_Buffer controlled_buffer_16
  assign OUT = decoder_1_out12 ? and_1_out : 16'bz;  // Controlled_Buffer controlled_buffer_17
  assign OUT = decoder_1_out13 ? or_1_out : 16'bz;  // Controlled_Buffer controlled_buffer_18
  assign OUT = decoder_1_out14 ? xor_1_out : 16'bz;  // Controlled_Buffer controlled_buffer_19
  assign OUT = decoder_1_out15 ? nand_1_out : 16'bz;  // Controlled_Buffer controlled_buffer_20
  assign OUT = decoder_1_out16 ? nor_1_out : 16'bz;  // Controlled_Buffer controlled_buffer_21
  assign OUT = decoder_1_out17 ? xnor_1_out : 16'bz;  // Controlled_Buffer controlled_buffer_22
  assign F_OUT = decoder_1_out18 ? comparator_1_eq : 1'bz;  // Controlled_Buffer controlled_buffer_23
  assign F_OUT = decoder_1_out19 ? ~comparator_1_eq : 1'bz;  // Controlled_Inverter controlled_inverter_1
  assign F_OUT = decoder_1_out20 ? comparator_1_lt : 1'bz;  // Controlled_Buffer controlled_buffer_24
  assign F_OUT = decoder_1_out21 ? comparator_1_gt : 1'bz;  // Controlled_Buffer controlled_buffer_25
  assign F_OUT = decoder_1_out22 ? comparator_2_eq : 1'bz;  // Controlled_Buffer controlled_buffer_26
  assign F_OUT = decoder_1_out23 ? ~comparator_2_eq : 1'bz;  // Controlled_Inverter controlled_inverter_2
  assign F_OUT = decoder_1_out24 ? comparator_2_lt : 1'bz;  // Controlled_Buffer controlled_buffer_27
  assign F_OUT = decoder_1_out25 ? comparator_2_gt : 1'bz;  // Controlled_Buffer controlled_buffer_28
  assign F_OUT = decoder_1_out11 ? not_2_out : 1'bz;  // Controlled_Buffer controlled_buffer_29
  assign F_OUT = decoder_1_out12 ? and_2_out : 1'bz;  // Controlled_Buffer controlled_buffer_30
  assign F_OUT = decoder_1_out13 ? or_2_out : 1'bz;  // Controlled_Buffer controlled_buffer_31
  assign F_OUT = decoder_1_out14 ? xor_2_out : 1'bz;  // Controlled_Buffer controlled_buffer_32
  assign F_OUT = decoder_1_out15 ? nand_2_out : 1'bz;  // Controlled_Buffer controlled_buffer_33
  assign F_OUT = decoder_1_out16 ? nor_2_out : 1'bz;  // Controlled_Buffer controlled_buffer_34
  assign F_OUT = decoder_1_out17 ? xnor_2_out : 1'bz;  // Controlled_Buffer controlled_buffer_35
  Decoder #(.select(5)) decoder_2 (
    .sel(OP[4:0]), .en(OP[5]));  // open: out0, out1, out2, out3, out4, out5, out6, out7, out8, out9, out10, out11, out12, out13, out14, out15, out16, out17, out18, out19, out20, out21, out22, out23, out24, out25, out26, out27, out28, out29, out30, out31
  Pull_Resistor pull_resistor_17 (.node(F_OUT));
  Pull_Resistor pull_resistor_18 (.node(OUT));

  // Notes on the sheet:
  //   Arithmetic
  //   Bitwise logic
  //   Comparison
endmodule
