// Logisim project CPU2.circ as structural Verilog: 2 circuits, main circuit main
module main (
  output [31:0] out_1
);

  wire AluA_EnableSigned, AluA_Left_UseConst, AluA_Right_UseConst, AluA_WriteOutput, and_1_out, and_2_out,
       and_3_out, and_5_out, big_rom_1_p1, big_rom_1_p2, buffer_1_out, CLK, clock_1_out, comparator_1_eq,
       comparator_1_gt, comparator_1_lt, comparator_2_eq, comparator_2_gt, comparator_2_lt, DoJump,
       DoJump_IfCompare_AluA, DoMicroJump, DoMicroJump_IfCompare_AluA, HALT, JumpDest_PlusOne,
       JumpDest_UseReg, JumpDest_UseRom, LoadInsn, LoadInsn_Direct, LoadInsn_IfJump, mini_bit_extender_5_p1,
       mini_bit_extender_6_p1, mini_bit_selector_5_p11, mini_bit_selector_5_p13, MovByte_Write,
       MovRam_Addr_UsePayload, MovRam_Addr_UseReg, MovRam_WriteFromRam, MovRam_WriteToRam, MovRegisters_A,
       MovRegisters_B, MovRom_Write, MovTiny_Write, multiplexer_2_out, multiplexer_3_out, not_1_out,
       not_2_out, not_3_out, not_4_out, not_5_out, not_6_out, not_7_out, or_2_out, or_4_out, or_6_out,
       or_7_out, ProgramCounter_Advance, pull_resistor_1_node, pull_resistor_5_node, pull_resistor_6_node,
       pull_resistor_8_node, s_r_ff_1_qn, ShouldMicroJump, ShouldPCJump, xor_1_out;
  wire [1:0] AluA_LeftConst_PayloadField, AluA_LeftReg_PayloadField, AluA_Op_PayloadField,
       AluA_OutReg_PayloadField, AluA_RightConst_PayloadField, AluA_RightReg_PayloadField,
       JumpCompare_AluAOp_Field, JumpDest_Reg_PayloadField, MovRam_AddrReg_PayloadField,
       MovRam_DataReg_PayloadField, MovRom_Reg_PayloadField, ProgramCounter_Advance_By;
  wire [2:0] JumpCompare_AluAOp, LoadInsn_Source, MicroJumpCompare_AluAOp, Prefetch_Source;
  wire [4:0] AluA_LeftConst, AluA_LeftReg, AluA_Op, AluA_OutReg, AluA_RightConst, AluA_RightReg,
       JumpDest_Reg, MicroJump_Dest, MovRam_AddrReg, MovRam_DataReg, MovReg_DstA, MovReg_DstB, MovReg_SrcA,
       MovReg_SrcB, MovRom_Reg, MovTinyA_Reg, MovTinyB_Reg;
  wire [7:0] counter_2_q;
  wire [14:0] RamAddr;
  wire [15:0] mini_bit_selector_1_p2, PC, PC_Next, Prefetch_RomAddr;
  wire [19:0] InsnPayload;
  wire [31:0] adder_2_out, AluA_LeftReg_Value, AluA_LeftValue, AluA_Result, AluA_RightReg_Value,
       AluA_RightValue, controlled_buffer_2_out, controlled_buffer_4_out, controlled_buffer_5_out, JumpDest,
       LoadInsn_Value, MovByte_Value, MovTinyA_Value, MovTinyB_Value, Prefetch_RomValue,
       pull_resistor_2_node, pull_resistor_3_node, pull_resistor_4_node, RamToRegValue, RegToRamValue,
       RomValue;
  wire [31:20] IR_q;

  // Mini_Bit_Selector #(.in_width(32), .out_width(16)) mini_bit_selector_1: pin names not known; wires that end beside it: JumpDest, mini_bit_selector_1_p2
  Pull_Resistor #(.pull(1)) pull_resistor_1 (.node(pull_resistor_1_node));
  Multiplexer #(.select(3), .width(16), .enable("false")) multiplexer_1 (
    .in0(PC), .in1(mini_bit_selector_1_p2), .in2(PC_Next), .out(Prefetch_RomAddr), .sel(Prefetch_Source));  // open: in3, in4, in5, in6, in7
  Adder #(.width(16)) adder_1 (.a(PC), .out(PC_Next), .cin(pull_resistor_1_node));  // open: b, cout
  Pull_Resistor pull_resistor_2 (.node(pull_resistor_2_node));
  ROM #(.addrWidth(16), .dataWidth(32), .sourcepath("asm/out.hex")) rom_1 (
    .addr(Prefetch_RomAddr), .data(Prefetch_RomValue));
  Comparator #(.width(32), .mode("unsigned")) comparator_1 (
    .a(AluA_Result), .b(pull_resistor_2_node), .gt(comparator_1_gt), .eq(comparator_1_eq),
    .lt(comparator_1_lt));
  Pull_Resistor pull_resistor_3 (.node(pull_resistor_3_node));
  not not_1 (not_1_out, comparator_1_gt);
  not not_2 (not_2_out, comparator_1_lt);
  Multiplexer #(.select(3), .enable("false")) multiplexer_2 (
    .in0(comparator_1_gt), .in1(not_1_out), .in2(comparator_1_eq), .in3(not_2_out), .in4(comparator_1_lt),
    .in5(not_3_out), .out(multiplexer_2_out), .sel(MicroJumpCompare_AluAOp));  // open: in6, in7
  not not_3 (not_3_out, comparator_1_eq);
  Comparator #(.width(32), .mode("unsigned")) comparator_2 (
    .a(AluA_Result), .b(pull_resistor_3_node), .gt(comparator_2_gt), .eq(comparator_2_eq),
    .lt(comparator_2_lt));
  and and_1 (and_1_out, multiplexer_2_out, DoMicroJump_IfCompare_AluA);
  not not_4 (not_4_out, comparator_2_gt);
  not not_5 (not_5_out, comparator_2_lt);
  Multiplexer #(.select(3), .enable("false")) multiplexer_3 (
    .in0(comparator_2_gt), .in1(not_4_out), .in2(comparator_2_eq), .in3(not_5_out), .in4(comparator_2_lt),
    .in5(not_6_out), .out(multiplexer_3_out), .sel(JumpCompare_AluAOp));  // open: in6, in7
  not not_6 (not_6_out, comparator_2_eq);
  // Splitter #(.appear("center"), .spacing("double")) splitter_1: pin names not known; wires that end beside it: ProgramCounter_Advance_By
  or or_1 (ShouldMicroJump, and_1_out, DoMicroJump, LoadInsn);
  Clock clock_1 (.out(clock_1_out));
  buf buffer_1 (buffer_1_out, clock_1_out);
  S_R_Flip_Flop s_r_ff_1 (.S(HALT), .Qn(s_r_ff_1_qn));  // open: R, clk, Q, reset, preset
  and and_2 (and_2_out, JumpDest_UseRom, ~ShouldPCJump);  // AND_Gate
  and and_3 (and_3_out, multiplexer_3_out, DoJump_IfCompare_AluA);
  // OR_Gate or_2 has open pins: out=or_2_out
  xor xor_1 (xor_1_out, clock_1_out, buffer_1_out);
  and and_4 (CLK, xor_1_out, s_r_ff_1_qn);
  Adder #(.width(32)) adder_2 (
    .a(JumpDest), .b(pull_resistor_4_node), .out(adder_2_out), .cin(JumpDest_PlusOne));  // open: cout
  Pull_Resistor pull_resistor_4 (.node(pull_resistor_4_node));
  or or_3 (ShouldPCJump, and_3_out, DoJump, or_2_out);
  ROM #(.addrWidth(16), .dataWidth(32), .sourcepath("asm/out.hex")) PROG (.addr(PC), .data(RomValue));
  Counter #(.width(16), .max('hffff)) counter_1 (
    .load(ShouldPCJump), .up(pull_resistor_5_node), .count(or_4_out), .clk(CLK), .Q(PC));  // open: clr, D, carry
  Pull_Resistor #(.pull(1)) pull_resistor_5 (.node(pull_resistor_5_node));
  or or_4 (or_4_out, ProgramCounter_Advance, and_2_out);
  // Mini_Bit_Selector #(.in_width(32), .out_width(16)) mini_bit_selector_2: pin names not known; wires that end beside it: adder_2_out
  Counter counter_2 (
    .load(ShouldMicroJump), .up(pull_resistor_6_node), .count(not_7_out), .clk(CLK), .Q(counter_2_q));  // open: clr, D, carry
  Pull_Resistor #(.pull(1)) pull_resistor_6 (.node(pull_resistor_6_node));
  not not_7 (not_7_out, ShouldMicroJump);
  // Mini_Bit_Extender #(.in_width(5), .out_width(8), .\type ("zero")) mini_bit_extender_1: pin names not known; wires that end beside it: MicroJump_Dest
  Register #(.width(32)) IR (.D(LoadInsn_Value), .en(LoadInsn), .clk(CLK), .Q({IR_q, InsnPayload}));  // open: clr
  assign JumpDest = JumpDest_UseRom ? RomValue : 32'bz;  // Controlled_Buffer controlled_buffer_1
  RAM #(.addrWidth(15), .dataWidth(32), .databus("bibus")) ram_1 (
    .addr(RamAddr), .we(MovRam_WriteToRam), .oe(MovRam_WriteFromRam), .clk(CLK), .din(RegToRamValue),
    .dout(RamToRegValue));
  and and_5 (and_5_out, LoadInsn_IfJump, ShouldPCJump);
  // Big_ROM #(.addressWidth(20), .valueWidth(64), .sourcepath("run/out/v2/microcode.hex")) big_rom_1: pin names not known; wires that end beside it: big_rom_1_p1, big_rom_1_p2
  // Splitter #(.fanout(32), .incoming(32), .appear("right"), .spacing("double")) splitter_2: pin names not known; wires that end beside it: big_rom_1_p1, HALT, LoadInsn_Direct
  // Splitter #(.appear("center"), .spacing("double")) splitter_3: pin names not known; wires that end beside it: ProgramCounter_Advance, MovRom_Write, MovRom_Reg_PayloadField
  // Splitter #(.appear("center"), .spacing("double")) splitter_4: pin names not known; wires that end beside it: AluA_LeftReg_PayloadField
  // Splitter #(.appear("center"), .spacing("double")) splitter_5: pin names not known; wires that end beside it: AluA_RightReg_PayloadField
  // Splitter #(.appear("center"), .spacing("double")) splitter_6: pin names not known; wires that end beside it: AluA_OutReg_PayloadField
  // Splitter #(.appear("center"), .spacing("double")) splitter_7: pin names not known; wires that end beside it: AluA_EnableSigned, AluA_WriteOutput, DoJump, AluA_Op_PayloadField
  // Splitter #(.appear("center"), .spacing("double")) splitter_8: pin names not known; wires that end beside it: JumpDest_UseRom, JumpDest_UseReg, MovByte_Write, MovTiny_Write, JumpDest_Reg_PayloadField
  // Splitter #(.appear("center"), .spacing("double")) splitter_9: pin names not known; wires that end beside it: DoJump_IfCompare_AluA, MovRam_WriteToRam, MovRam_WriteFromRam, JumpCompare_AluAOp_Field
  // Splitter #(.appear("center"), .spacing("double")) splitter_10: pin names not known; wires that end beside it: MovRam_Addr_UsePayload, MovRam_Addr_UseReg, MovRam_DataReg_PayloadField
  or or_5 (LoadInsn, LoadInsn_Direct, and_5_out);
  Pull_Resistor pull_resistor_7 (.node(LoadInsn_Source));
  Multiplexer #(.select(3), .width(32), .enable("false")) multiplexer_4 (
    .in0(RomValue), .in1(Prefetch_RomValue), .out(LoadInsn_Value), .sel(LoadInsn_Source));  // open: in2, in3, in4, in5, in6, in7
  // Splitter #(.fanout(32), .incoming(32), .appear("right"), .spacing("double")) splitter_11: pin names not known; wires that end beside it: big_rom_1_p2
  // Splitter #(.appear("center"), .spacing("double")) splitter_12: pin names not known; wires that end beside it: MovRam_AddrReg_PayloadField
  // Splitter #(.appear("center"), .spacing("double")) splitter_13: pin names not known; wires that end beside it: AluA_LeftConst_PayloadField
  // Splitter #(.appear("center"), .spacing("double")) splitter_14: pin names not known; wires that end beside it: AluA_Left_UseConst, AluA_Right_UseConst, MovRegisters_A, AluA_RightConst_PayloadField
  // Splitter #(.fanout(3), .incoming(3), .appear("center"), .spacing("double")) splitter_15: pin names not known; wires that end beside it: MovRegisters_B, Prefetch_Source
  // Splitter #(.appear("center"), .spacing("double")) splitter_16: pin names not known; wires that end beside it: JumpDest_PlusOne, ProgramCounter_Advance_By
  // Splitter #(.fanout(3), .incoming(3), .appear("center"), .spacing("double")) splitter_17: pin names not known; wires that end beside it: LoadInsn_IfJump, LoadInsn_Source
  // Splitter #(.fanout(5), .incoming(5), .appear("center"), .spacing("double")) splitter_18: pin names not known; wires that end beside it: DoMicroJump, MicroJump_Dest
  // Splitter #(.fanout(3), .incoming(3), .appear("center"), .spacing("double")) splitter_19: pin names not known; wires that end beside it: DoMicroJump_IfCompare_AluA, MicroJumpCompare_AluAOp
  // Splitter #(.appear("center"), .spacing("double")) splitter_20: pin names not known; wires that end beside it: ProgramCounter_Advance_By
  or or_6 (or_6_out, AluA_WriteOutput, DoJump_IfCompare_AluA);
  // OR_Gate or_7 has open pins: out=or_7_out
  Pull_Resistor #(.pull(1)) pull_resistor_8 (.node(pull_resistor_8_node));
  // Mini_Bit_Extender #(.in_width(2), .\type ("zero")) mini_bit_extender_2: pin names not known
  Adder #(.width(16)) adder_3 (.b(PC), .cin(pull_resistor_8_node));  // open: a, out, cout
  // Mini_Bit_Extender #(.in_width(16), .out_width(32)) mini_bit_extender_3: pin names not known
  Pull_Resistor pull_resistor_9 (.node(AluA_LeftValue));
  // ALU #(.width(32)) alu_1: pin names not known; wires that end beside it: AluA_EnableSigned, AluA_Op, AluA_LeftValue, AluA_RightValue, AluA_Result
  // Probe on controlled_buffer_2_out
  // Probe on controlled_buffer_2_out
  assign controlled_buffer_2_out = or_6_out ? AluA_LeftValue : 32'bz;  // Controlled_Buffer controlled_buffer_2
  Controlled_Buffer #(.width(32)) controlled_buffer_3 (.out(JumpDest), .en(or_7_out));  // open: in
  Pull_Resistor pull_resistor_10 (.node(AluA_RightValue));
  // Probe on controlled_buffer_4_out
  assign controlled_buffer_4_out = or_6_out ? AluA_RightValue : 32'bz;  // Controlled_Buffer controlled_buffer_4
  // Probe on controlled_buffer_4_out
  // Probe on controlled_buffer_5_out
  assign controlled_buffer_5_out = or_6_out ? AluA_Result : 32'bz;  // Controlled_Buffer controlled_buffer_5
  // Probe on controlled_buffer_5_out
  // Splitter #(.fanout(4), .incoming(20), .appear("center"), .spacing("double"), .bit1(0), .bit2(0), .bit3(0), .bit4(0), .bit5(1), .bit6(1), .bit7(1), .bit8(1), .bit9(1), .bit10(2), .bit11(2), .bit12(2), .bit13(2), .bit14(2), .bit15(3), .bit16(3), .bit17(3), .bit18(3), .bit19(3)) splitter_21: pin names not known; wires that end beside it: InsnPayload, MovTinyB_Reg, MovTinyA_Reg
  // Mini_Bit_Selector #(.in_width(20), .out_width(15)) mini_bit_selector_3: pin names not known; wires that end beside it: InsnPayload
  // Splitter #(.fanout(4), .incoming(20), .appear("center"), .spacing("double"), .bit1(0), .bit2(0), .bit3(0), .bit4(0), .bit5(1), .bit6(1), .bit7(1), .bit8(1), .bit9(1), .bit10(2), .bit11(2), .bit12(2), .bit13(2), .bit14(2), .bit15(3), .bit16(3), .bit17(3), .bit18(3), .bit19(3)) splitter_22: pin names not known; wires that end beside it: InsnPayload, MovReg_DstB, MovReg_SrcB, MovReg_DstA, MovReg_SrcA
  Multiplexer #(.select(2), .width(5), .enable("false")) multiplexer_5 (
    .in0(InsnPayload[4:0]), .in1(InsnPayload[9:5]), .in2(InsnPayload[14:10]), .in3(InsnPayload[19:15]),
    .out(MovRom_Reg), .sel(MovRom_Reg_PayloadField));
  Multiplexer #(.select(2), .width(5), .enable("false")) multiplexer_6 (
    .in0(InsnPayload[4:0]), .in1(InsnPayload[9:5]), .in2(InsnPayload[14:10]), .in3(InsnPayload[19:15]),
    .out(AluA_LeftReg), .sel(AluA_LeftReg_PayloadField));
  Multiplexer #(.select(2), .width(5), .enable("false")) multiplexer_7 (
    .in0(InsnPayload[4:0]), .in1(InsnPayload[9:5]), .in2(InsnPayload[14:10]), .in3(InsnPayload[19:15]),
    .out(AluA_RightReg), .sel(AluA_RightReg_PayloadField));
  Multiplexer #(.select(2), .width(5), .enable("false")) multiplexer_8 (
    .in0(InsnPayload[4:0]), .in1(InsnPayload[9:5]), .in2(InsnPayload[14:10]), .in3(InsnPayload[19:15]),
    .out(AluA_OutReg), .sel(AluA_OutReg_PayloadField));
  Multiplexer #(.select(2), .width(5), .enable("false")) multiplexer_9 (
    .in0(InsnPayload[4:0]), .in1(InsnPayload[9:5]), .in2(InsnPayload[14:10]), .in3(InsnPayload[19:15]),
    .out(AluA_Op), .sel(AluA_Op_PayloadField));
  Multiplexer #(.select(2), .width(5), .enable("false")) multiplexer_10 (
    .in0(InsnPayload[4:0]), .in1(InsnPayload[9:5]), .in2(InsnPayload[14:10]), .in3(InsnPayload[19:15]),
    .out(JumpDest_Reg), .sel(JumpDest_Reg_PayloadField));
  Multiplexer #(.select(2), .width(5), .enable("false")) multiplexer_11 (
    .in0(InsnPayload[4:0]), .in1(InsnPayload[9:5]), .in2(InsnPayload[14:10]), .in3(InsnPayload[19:15]),
    .out(AluA_LeftConst), .sel(AluA_LeftConst_PayloadField));
  Multiplexer #(.select(2), .width(5), .enable("false")) multiplexer_12 (
    .in0(InsnPayload[4:0]), .in1(InsnPayload[9:5]), .in2(InsnPayload[14:10]), .in3(InsnPayload[19:15]),
    .out(AluA_RightConst), .sel(AluA_RightConst_PayloadField));
  // Mini_Bit_Extender #(.out_width(32)) mini_bit_extender_4: pin names not known; wires that end beside it: InsnPayload[7:0], MovByte_Value
  // Mini_Bit_Extender #(.in_width(5), .out_width(32)) mini_bit_extender_5: pin names not known; wires that end beside it: mini_bit_extender_5_p1, mini_bit_extender_5_p1, MovTinyB_Value
  // Mini_Bit_Extender #(.in_width(5), .out_width(32)) mini_bit_extender_6: pin names not known; wires that end beside it: mini_bit_extender_6_p1, mini_bit_extender_6_p1, MovTinyA_Value
  Controlled_Buffer #(.width(15)) controlled_buffer_6 (.out(RamAddr), .en(MovRam_Addr_UsePayload));  // open: in
  Multiplexer #(.select(2), .width(5), .enable("false")) multiplexer_13 (
    .in0(InsnPayload[4:0]), .in1(InsnPayload[9:5]), .in2(InsnPayload[14:10]), .in3(InsnPayload[19:15]),
    .out(MovRam_AddrReg), .sel(MovRam_AddrReg_PayloadField));
  Multiplexer #(.select(2), .width(5), .enable("false")) multiplexer_14 (
    .in0(InsnPayload[4:0]), .in1(InsnPayload[9:5]), .in2(InsnPayload[14:10]), .in3(InsnPayload[19:15]),
    .out(MovRam_DataReg), .sel(MovRam_DataReg_PayloadField));
  Multiplexer #(.select(2), .width(5), .enable("false")) multiplexer_15 (
    .in0(InsnPayload[4:0]), .in1(InsnPayload[9:5]), .in2(InsnPayload[14:10]), .in3(InsnPayload[19:15]),
    .sel(JumpCompare_AluAOp_Field));  // open: out
  // Mini_Bit_Selector #(.in_width(5), .out_width(3)) mini_bit_selector_4: pin names not known; wires that end beside it: JumpCompare_AluAOp
  Multiplexer #(.width(32), .enable("false")) multiplexer_16 (
    .in0(AluA_LeftReg_Value), .out(AluA_LeftValue), .sel(AluA_Left_UseConst));  // open: in1
  // Mini_Bit_Extender #(.in_width(5), .out_width(32)) mini_bit_extender_7: pin names not known; wires that end beside it: AluA_LeftConst
  Multiplexer #(.width(32), .enable("false")) multiplexer_17 (
    .in0(AluA_RightReg_Value), .out(AluA_RightValue), .sel(AluA_Right_UseConst));  // open: in1
  // Mini_Bit_Extender #(.in_width(5), .out_width(32)) mini_bit_extender_8: pin names not known; wires that end beside it: AluA_RightConst
  // Register_Bank #(.width(32), .registerCount(32), .portCount(32)) register_bank_1: pin names not known; wires that end beside it: JumpDest_Reg, AluA_OutReg, AluA_RightReg, AluA_LeftReg, MovRom_Reg, CLK, MovByte_Value, AluA_WriteOutput, AluA_Result, MovRom_Write, RomValue, out_1, AluA_RightReg_Value, AluA_LeftReg_Value
  // Mini_Bit_Selector #(.in_width(32), .out_width(15)) mini_bit_selector_5: pin names not known; wires that end beside it: MovReg_DstB, MovReg_SrcB, MovReg_DstA, MovReg_SrcA, MovRam_AddrReg, MovRam_DataReg, MovTinyB_Reg, MovTinyA_Reg, InsnPayload[19:15], MovRegisters_B, mini_bit_selector_5_p11, MovRegisters_A, mini_bit_selector_5_p13, MovRam_WriteFromRam, RamToRegValue, MovTiny_Write, MovTinyB_Value, MovTiny_Write, MovTinyA_Value, RegToRamValue, mini_bit_selector_5_p11, mini_bit_selector_5_p13, MovRam_Addr_UseReg, JumpDest_UseReg, JumpDest, RamAddr

  // Other names for the same wires on the sheet: MovByte_Reg[4:0] = InsnPayload[19:15]

  // Notes on the sheet:
  //   contents of rom_1 (hex, n*v repeats v):
  //   409841 e08800 308001 310000 b00441 b38424 1018800 b00822 820462 3 8b0c82 6 e09800 b01826 1108000
  //   700000 3
  //   contents of PROG (hex, n*v repeats v):
  //   409841 e08800 308001 310000 b00441 b38424 1018800 b00822 820462 3 8b0c82 6 e09800 b01826 1108000
  //   700000 3
  //   ±
  //   +
  //   =
endmodule

module viewer (
);

  wire [31:0] main_1_out_1;

  main main_1 (.out_1(main_1_out_1));
  // Probe on main_1_out_1
endmodule
